# Fritzing sketch HSUSensor (saved by Fritzing 0.7.10b)
breadboards: 1

parts:
  J1 = Generic male header - 7 pins [package=THT]
  MLX90614 = MLX90614 Infrared Thermometer
  R1 = Resistor [tolerance=±5% resistance=4.7k package=THT]
  R2 = Resistor [tolerance=±5% resistance=4.7k package=THT]
  C1 = Ceramic Capacitor [capacitance=0.1µF package="100 mil [THT, multilayer]"]
  U1 = TSL235R [package=THT]
  LED2 = LED - 5mm [color="Infrared (940nm)" package="5 mm [THT]"]
  LED1 = LED - 5mm [color="Red (633nm)" package="5 mm [THT]"]

nets:
  N1: J1.pin1, MLX90614.VDD, R1.Pin_0, R2.Pin_0, C1.0, U1.2
  N2: J1.pin2, MLX90614.VSS, C1.1, U1.1, LED2.cathode, LED1.cathode
  N3: J1.pin3, MLX90614.SCL_/_Vz, R2.Pin_1
  N4: J1.pin4, MLX90614.PWM_/_SDA, R1.Pin_1
  N5: J1.pin5, LED1.anode
  N6: J1.pin6, LED2.anode
  N7: J1.pin7, U1.3

notes:
  HSU Sensor Board v1.0
  GND
  Medical Tricorder HSU Sensor Board, This Schematic is incomplete, 1.5

custom parts:
  MLX90614 Infrared Thermometer: The MLX90614 is an Infra Red thermometer for non contact temperature measurements. Both the IR sensitive thermopile detector chip and the signal conditioning ASSP are integrated in the same TO-39 can.
  TSL235R: A generic part converted to a TSL235R.
