# Fritzing sketch TCHandScanner (saved by Fritzing 0.7.10b)
breadboards: 1

parts:
  Nano = Arduino Nano v3.0
  JY-MCU = Generic female header - 4 pins [package=THT]
  R1 = 10k Ω Resistor [package=THT]
  R2 = 10k Ω Resistor [package=THT]
  VCC_(9V) = Battery block 9V
  S1 = Pushbutton [package="[THT]"]
  R3 = 10k Ω Resistor [package=THT]

nets:
  N1: Nano.GND, JY-MCU.pin3, VCC_(9V).-, R3.Pin_1
  N2: Nano.D2, R2.Pin_0
  N3: Nano.D3, R1.Pin_0
  N4: Nano.D4, S1.Pin_3, S1.Pin_4, R3.Pin_0
  N5: Nano.D7, JY-MCU.pin4
  N6: Nano.+5V, S1.Pin_1, S1.Pin_2
  N7: Nano.VIN, VCC_(9V).+
  N8: JY-MCU.pin1, R1.Pin_1
  N9: JY-MCU.pin2, R2.Pin_1
